# Fritzing sketch nanorover (saved by Fritzing 0.9.3b)
breadboards: 1

parts:
  Part1 = Arduino Nano (Rev3.0)
  J1 = Basic Servo
  J2 = Basic Servo
  Part2 = SRF05 Ultrasonic Rangefinder
  VCC1 = 4 x AAA Battery Mount

nets:
  GND: Part1.GND, J1.gnd, J2.gnd, Part2.GND, VCC1.-
  N1: Part1.D2, J1.pulse
  N2: Part1.D4, J2.pulse
  N3: Part1.D12/MISO, Part2.Echo
  VCC: Part1.VIN, Part1.5V, J1.vcc, J2.vcc, Part2.VCC, VCC1.+
  N4: Part1.D13/SCK, Part2.Trig
